// Logisim project pipeline.circ as structural Verilog
module Pipeline (
);

  wire branch_unit_1_branch_output, clock_1_out, ex_mem_1_mem_read_2, ex_mem_1_mem_write_2,
       ex_mem_1_reg_write_2, hazard_detection_unit_1_disable_if_id, hazard_detection_unit_1_disable_pc,
       hazard_detection_unit_1_zeroing_control_signals, id_ex_1_branch_imm_type_2, id_ex_1_ext_op_2,
       id_ex_1_ext_type_2, id_ex_1_j_2, id_ex_1_mem_read_2, id_ex_1_mem_write_2, id_ex_1_reg_write_2,
       id_ex_1_set_type_2, main_control_1_branch_imm_type, main_control_1_branch_jump, main_control_1_ext_op,
       main_control_1_ext_type, main_control_1_j, main_control_1_link_reg, main_control_1_mem_read,
       main_control_1_mem_write, main_control_1_reg_read_ra, main_control_1_reg_read_rb,
       main_control_1_reg_write, main_control_1_set_type, mem_wb_1_reg_write_2, n32_bit_alu_unit_1_sign_flag,
       n32_bit_alu_unit_1_zero_flag, not_1_out;
  wire [1:0] ex_mem_1_reg_src_2, id_ex_1_alu_src_2, id_ex_1_pc_src_2, id_ex_1_reg_src_2, if_id_1_fn,
       main_control_1_alu_src, main_control_1_pc_src, main_control_1_reg_src, mem_wb_1_reg_src_2;
  wire [2:0] ex_mem_1_dest_reg_2, forwarding_unit_1_forwarda, forwarding_unit_1_forwardb,
       id_ex_1_branch_type_2, id_ex_1_dest_reg_2, id_ex_1_ra_2, id_ex_1_rb_2, if_id_1_rd, if_id_1_rs,
       if_id_1_rt, main_control_1_branch_type, mem_wb_1_dest_reg_2, multiplexer_1_out, multiplexer_2_out,
       multiplexer_3_out;
  wire [4:0] if_id_1_op_code;
  wire [7:0] id_ex_1_alu_control_2, id_ex_1_imm_5_8_2, if_id_1_imm_5_8, main_control_1_alu_control;
  wire [10:0] id_ex_1_imm11_2, if_id_1_imm_11;
  wire [11:0] n32_bit_alu_unit_1_alu_output_2;
  wire [15:0] instruction_memory_1_instruction;
  wire [19:0] ex_mem_1_pc_2_2, id_ex_1_pc_1_2, if_id_1_pc_1_2, instruction_memory_1_pc_1,
       n32_bit_alu_unit_1_alu_output, next_pc_unit_1_next_pc;
  wire [31:0] bit_extender_1_out, data_memory_1_data_out, ex_mem_1_alu_output_2, ex_mem_1_set_unit_output_2,
       ex_mem_1_sw_data_2, extend_unit_1_extended_output, id_ex_1_a_2, id_ex_1_b_2, mem_wb_1_alu_output_2,
       mem_wb_1_data_out_2, mem_wb_1_extended_pc_2_2, mem_wb_1_set_unit_output_2, multiplexer_4_out,
       multiplexer_5_out, multiplexer_6_out, multiplexer_7_out, register_file_1_clk_2, register_file_1_clk_3,
       set_unit_1_set_output;

  Clock clock_1 (.out(clock_1_out));
  Instruction_Memory instruction_memory_1 (
    .next_pc(next_pc_unit_1_next_pc), .ALU_output_20bitLSB(n32_bit_alu_unit_1_alu_output),
    .Instruction(instruction_memory_1_instruction), .PC_SRC(id_ex_1_pc_src_2), .clk(clock_1_out),
    .PC_1(instruction_memory_1_pc_1), .Enable(not_1_out));
  IF_ID if_id_1 (
    .instruction(instruction_memory_1_instruction), .imm_11(if_id_1_imm_11), .imm_5_8(if_id_1_imm_5_8),
    .fn(if_id_1_fn), .Rt(if_id_1_rt), .Rs(if_id_1_rs), .Rd(if_id_1_rd), .OP_code(if_id_1_op_code),
    .clk(clock_1_out), .pc_1(instruction_memory_1_pc_1), .pc_1_2(if_id_1_pc_1_2),
    .Clear(hazard_detection_unit_1_disable_if_id));
  Main_Control main_control_1 (
    .Op_code_5bit(if_id_1_op_code), .REG_READ_RA(main_control_1_reg_read_ra),
    .REG_READ_RB(main_control_1_reg_read_rb), .LINK_REG(main_control_1_link_reg),
    .REG_WRITE(main_control_1_reg_write), .EXT_OP(main_control_1_ext_op), .EXT_TYPE(main_control_1_ext_type),
    .ALU_SRC(main_control_1_alu_src), .function_2bit(if_id_1_fn), .ALU_CONTROL(main_control_1_alu_control),
    .MEM_READ(main_control_1_mem_read), .MEM_WRITE(main_control_1_mem_write),
    .SET_TYPE(main_control_1_set_type), .REG_SRC(main_control_1_reg_src),
    .BRANCH_TYPE(main_control_1_branch_type), .BRANCH_IMM_TYPE(main_control_1_branch_imm_type),
    .J(main_control_1_j), .PC_SRC(main_control_1_pc_src), .BRANCH_JUMP(main_control_1_branch_jump));
  not not_1 (not_1_out, hazard_detection_unit_1_disable_pc);
  Multiplexer #(.width(3), .enable("false")) multiplexer_1 (
    .in0(if_id_1_rs), .in1(if_id_1_rd), .out(multiplexer_1_out), .sel(main_control_1_reg_read_ra));
  Multiplexer #(.width(3), .enable("false")) multiplexer_2 (
    .in0(if_id_1_rt), .in1(if_id_1_rd), .out(multiplexer_2_out), .sel(main_control_1_reg_read_rb));
  Multiplexer #(.width(3), .enable("false")) multiplexer_3 (
    .in0(if_id_1_rd), .in1(3'b111), .out(multiplexer_3_out), .sel(main_control_1_link_reg));
  Hazard_detection_unit hazard_detection_unit_1 (
    .ID_EX_MEM_READ(id_ex_1_mem_read_2), .IF_ID_RA(multiplexer_1_out), .ID_EX_dest_reg(id_ex_1_dest_reg_2),
    .IF_ID_RB(multiplexer_2_out), .IF_ID_ALU_SRC(main_control_1_alu_src),
    .zeroing_control_signals(hazard_detection_unit_1_zeroing_control_signals),
    .BRANCH_JUMP(main_control_1_branch_jump), .clk(clock_1_out),
    .Disable_PC(hazard_detection_unit_1_disable_pc), .Disable_IF_ID(hazard_detection_unit_1_disable_if_id));
  register_file register_file_1 (
    .clk_2(register_file_1_clk_2), .clk_3(register_file_1_clk_3), .data_in(multiplexer_7_out),
    .rd_or_rt_3bit_write(mem_wb_1_dest_reg_2), .RegWrite(mem_wb_1_reg_write_2), .clk(clock_1_out),
    .rs_or_rt_3bit_read(multiplexer_2_out), .rs_or_rt_3bit_read_2(multiplexer_1_out));
  ID_EX id_ex_1 (
    .pc_1(if_id_1_pc_1_2), .imm11(if_id_1_imm_11), .imm_5_8(if_id_1_imm_5_8), .A(register_file_1_clk_2),
    .B(register_file_1_clk_3), .dest_reg(multiplexer_3_out), .BRANCH_TYPE(main_control_1_branch_type),
    .pc_1_2(id_ex_1_pc_1_2), .imm11_2(id_ex_1_imm11_2), .imm_5_8_2(id_ex_1_imm_5_8_2), .A_2(id_ex_1_a_2),
    .B_2(id_ex_1_b_2), .dest_reg_2(id_ex_1_dest_reg_2), .BRANCH_TYPE_2(id_ex_1_branch_type_2),
    .clk(clock_1_out), .BRANCH_IMM_TYPE(main_control_1_branch_imm_type),
    .BRANCH_IMM_TYPE_2(id_ex_1_branch_imm_type_2), .J(main_control_1_j), .J_2(id_ex_1_j_2),
    .PC_SRC(main_control_1_pc_src), .PC_SRC_2(id_ex_1_pc_src_2), .REG_WRITE(main_control_1_reg_write),
    .REG_WRITE_2(id_ex_1_reg_write_2), .EXT_OP(main_control_1_ext_op), .EXT_OP_2(id_ex_1_ext_op_2),
    .EXT_TYPE(main_control_1_ext_type), .EXT_TYPE_2(id_ex_1_ext_type_2), .ALU_SRC(main_control_1_alu_src),
    .ALU_SRC_2(id_ex_1_alu_src_2), .ALU_CONTROL(main_control_1_alu_control),
    .ALU_CONTROL_2(id_ex_1_alu_control_2), .MEM_READ(main_control_1_mem_read),
    .MEM_READ_2(id_ex_1_mem_read_2), .MEM_WRITE(main_control_1_mem_write), .MEM_WRITE_2(id_ex_1_mem_write_2),
    .SET_TYPE(main_control_1_set_type), .SET_TYPE_2(id_ex_1_set_type_2), .REG_SRC(main_control_1_reg_src),
    .REG_SRC_2(id_ex_1_reg_src_2), .RA(multiplexer_1_out), .RA_2(id_ex_1_ra_2), .RB(multiplexer_2_out),
    .RB_2(id_ex_1_rb_2), .zeroing_control_singals(hazard_detection_unit_1_zeroing_control_signals));
  Extend_Unit extend_unit_1 (
    .Extended_output(extend_unit_1_extended_output), .EXT_OP(id_ex_1_ext_op_2),
    .EXT_TYPE(id_ex_1_ext_type_2), .imm_in(id_ex_1_imm_5_8_2));
  Multiplexer #(.select(2), .width(32), .enable("false")) multiplexer_4 (
    .in0(id_ex_1_b_2), .in1(extend_unit_1_extended_output), .in2(32'h8), .in3({32{1'b0}}),
    .out(multiplexer_4_out), .sel(id_ex_1_alu_src_2));
  Forwarding_Unit forwarding_unit_1 (
    .EX_MEM_dest_reg(ex_mem_1_dest_reg_2), .ID_EX_RA(id_ex_1_ra_2), .EX_MEM_REGWRITE(ex_mem_1_reg_write_2),
    .MEM_WB_REGWRITE(mem_wb_1_reg_write_2), .MEM_WB_dest_reg(mem_wb_1_dest_reg_2),
    .ALU_SRC(id_ex_1_alu_src_2), .ID_EX_RB(id_ex_1_rb_2), .ForwardA(forwarding_unit_1_forwarda),
    .ForwardB(forwarding_unit_1_forwardb), .EX_MEM_MEM_READ(ex_mem_1_mem_read_2));
  Multiplexer #(.select(3), .width(32), .enable("false")) multiplexer_5 (
    .in0(id_ex_1_a_2), .in1(multiplexer_7_out), .in2(ex_mem_1_alu_output_2), .in3(ex_mem_1_alu_output_2),
    .in4(data_memory_1_data_out), .out(multiplexer_5_out), .sel(forwarding_unit_1_forwarda));  // open: in5, in6, in7
  Multiplexer #(.select(3), .width(32), .enable("false")) multiplexer_6 (
    .in0(multiplexer_4_out), .in1(multiplexer_7_out), .in2(ex_mem_1_alu_output_2),
    .in3(ex_mem_1_alu_output_2), .in4(data_memory_1_data_out), .out(multiplexer_6_out),
    .sel(forwarding_unit_1_forwardb));  // open: in5, in6, in7
  Branch_Unit branch_unit_1 (
    .zero_flag(n32_bit_alu_unit_1_zero_flag), .sign_flag(n32_bit_alu_unit_1_sign_flag),
    .BRANCH_TYPE(id_ex_1_branch_type_2), .branch_output(branch_unit_1_branch_output));
  _32_bit_ALU_Unit u_32_bit_alu_unit_1 (
    .A(multiplexer_5_out), .B(multiplexer_6_out), .ALU_CONTROL(id_ex_1_alu_control_2),
    .ALU_output({n32_bit_alu_unit_1_alu_output_2, n32_bit_alu_unit_1_alu_output}),
    .Zero_flag(n32_bit_alu_unit_1_zero_flag), .sign_flag(n32_bit_alu_unit_1_sign_flag));  // open: Overflow_flag
  Next_PC_Unit next_pc_unit_1 (
    .pc_1(id_ex_1_pc_1_2), .branch_imm_8(id_ex_1_imm_5_8_2), .jump_imm_11(id_ex_1_imm11_2),
    .next_pc(next_pc_unit_1_next_pc), .BRANCH_IMM_TYPE(id_ex_1_branch_imm_type_2), .J(id_ex_1_j_2),
    .branch_output(branch_unit_1_branch_output));
  Set_unit set_unit_1 (
    .Extended_imm8(extend_unit_1_extended_output),
    .Alu_shifted_output({n32_bit_alu_unit_1_alu_output_2, n32_bit_alu_unit_1_alu_output}),
    .Set_output(set_unit_1_set_output), .SET_TYPE(id_ex_1_set_type_2));
  EX_MEM ex_mem_1 (
    .ALU_output({n32_bit_alu_unit_1_alu_output_2, n32_bit_alu_unit_1_alu_output}), .sw_data(id_ex_1_b_2),
    .dest_reg(id_ex_1_dest_reg_2), .REG_WRITE(id_ex_1_reg_write_2), .MEM_READ(id_ex_1_mem_read_2),
    .MEM_WRITE(id_ex_1_mem_write_2), .REG_SRC(id_ex_1_reg_src_2), .ALU_output_2(ex_mem_1_alu_output_2),
    .sw_data_2(ex_mem_1_sw_data_2), .dest_reg_2(ex_mem_1_dest_reg_2), .REG_WRITE_2(ex_mem_1_reg_write_2),
    .MEM_READ_2(ex_mem_1_mem_read_2), .MEM_WRITE_2(ex_mem_1_mem_write_2), .REG_SRC_2(ex_mem_1_reg_src_2),
    .clk(clock_1_out), .set_unit_output(set_unit_1_set_output),
    .set_unit_output_2(ex_mem_1_set_unit_output_2), .PC_2(id_ex_1_pc_1_2), .PC_2_2(ex_mem_1_pc_2_2));
  assign bit_extender_1_out = {{12{1'b0}}, ex_mem_1_pc_2_2};  // Bit_Extender bit_extender_1
  Data_memory data_memory_1 (
    .Address_in(ex_mem_1_alu_output_2), .data_out(data_memory_1_data_out), .MEM_WRITE(ex_mem_1_mem_write_2),
    .MEM_READ(ex_mem_1_mem_read_2), .data_in(ex_mem_1_sw_data_2), .clk(clock_1_out));
  MEM_WB mem_wb_1 (
    .data_out(data_memory_1_data_out), .data_out_2(mem_wb_1_data_out_2), .dest_reg(ex_mem_1_dest_reg_2),
    .dest_reg_2(mem_wb_1_dest_reg_2), .REG_WRITE(ex_mem_1_reg_write_2), .REG_WRITE_2(mem_wb_1_reg_write_2),
    .clk(clock_1_out), .REG_SRC(ex_mem_1_reg_src_2), .REG_SRC_2(mem_wb_1_reg_src_2),
    .extended_PC_2(bit_extender_1_out), .extended_PC_2_2(mem_wb_1_extended_pc_2_2),
    .ALU_output(ex_mem_1_alu_output_2), .ALU_output_2(mem_wb_1_alu_output_2),
    .set_unit_output(ex_mem_1_set_unit_output_2), .set_unit_output_2(mem_wb_1_set_unit_output_2));
  Multiplexer #(.select(2), .width(32), .enable("false")) multiplexer_7 (
    .in0(mem_wb_1_alu_output_2), .in1(mem_wb_1_set_unit_output_2), .in2(mem_wb_1_data_out_2),
    .in3(mem_wb_1_extended_pc_2_2), .out(multiplexer_7_out), .sel(mem_wb_1_reg_src_2));
endmodule

module single_32bit_register (
  input  [31:0] data_in,
  input  Load,
  input  clk,
  output [31:0] register_value
);

  wire and_1_out, and_2_out, and_3_out, and_4_out, and_5_out, and_6_out, and_7_out, and_8_out, and_9_out,
       and_10_out, and_11_out, and_12_out, and_13_out, and_14_out, and_15_out, and_16_out, and_17_out,
       and_18_out, and_19_out, and_20_out, and_21_out, and_22_out, and_23_out, and_24_out, and_25_out,
       and_26_out, and_27_out, and_28_out, and_29_out, and_30_out, and_31_out, and_32_out, and_33_out,
       and_34_out, and_35_out, and_36_out, and_37_out, and_38_out, and_39_out, and_40_out, and_41_out,
       and_42_out, and_43_out, and_44_out, and_45_out, and_46_out, and_47_out, and_48_out, and_49_out,
       and_50_out, and_51_out, and_52_out, and_53_out, and_54_out, and_55_out, and_56_out, and_57_out,
       and_58_out, and_59_out, and_60_out, and_61_out, and_62_out, and_63_out, and_64_out, not_1_out,
       not_2_out, not_3_out, not_4_out, not_5_out, not_6_out, not_7_out, not_8_out, not_9_out, not_10_out,
       not_11_out, not_12_out, not_13_out, not_14_out, not_15_out, not_16_out, not_17_out, not_18_out,
       not_19_out, not_20_out, not_21_out, not_22_out, not_23_out, not_24_out, not_25_out, not_26_out,
       not_27_out, not_28_out, not_29_out, not_30_out, not_31_out, not_32_out, or_1_out, or_2_out, or_3_out,
       or_4_out, or_5_out, or_6_out, or_7_out, or_8_out, or_9_out, or_10_out, or_11_out, or_12_out,
       or_13_out, or_14_out, or_15_out, or_16_out, or_17_out, or_18_out, or_19_out, or_20_out, or_21_out,
       or_22_out, or_23_out, or_24_out, or_25_out, or_26_out, or_27_out, or_28_out, or_29_out, or_30_out,
       or_31_out, or_32_out;

  not not_1 (not_1_out, Load);
  not not_2 (not_2_out, Load);
  not not_3 (not_3_out, Load);
  not not_4 (not_4_out, Load);
  not not_5 (not_5_out, Load);
  not not_6 (not_6_out, Load);
  not not_7 (not_7_out, Load);
  not not_8 (not_8_out, Load);
  not not_9 (not_9_out, Load);
  not not_10 (not_10_out, Load);
  not not_11 (not_11_out, Load);
  not not_12 (not_12_out, Load);
  not not_13 (not_13_out, Load);
  not not_14 (not_14_out, Load);
  not not_15 (not_15_out, Load);
  not not_16 (not_16_out, Load);
  and and_1 (and_1_out, register_value[0], not_17_out);
  not not_17 (not_17_out, Load);
  and and_2 (and_2_out, Load, data_in[0]);
  and and_3 (and_3_out, register_value[1], not_18_out);
  not not_18 (not_18_out, Load);
  and and_4 (and_4_out, Load, data_in[1]);
  and and_5 (and_5_out, register_value[2], not_19_out);
  not not_19 (not_19_out, Load);
  and and_6 (and_6_out, Load, data_in[2]);
  and and_7 (and_7_out, register_value[3], not_20_out);
  not not_20 (not_20_out, Load);
  and and_8 (and_8_out, Load, data_in[3]);
  and and_9 (and_9_out, register_value[4], not_21_out);
  not not_21 (not_21_out, Load);
  and and_10 (and_10_out, Load, data_in[4]);
  and and_11 (and_11_out, register_value[5], not_22_out);
  not not_22 (not_22_out, Load);
  and and_12 (and_12_out, Load, data_in[5]);
  and and_13 (and_13_out, register_value[6], not_23_out);
  not not_23 (not_23_out, Load);
  and and_14 (and_14_out, Load, data_in[6]);
  and and_15 (and_15_out, register_value[7], not_24_out);
  not not_24 (not_24_out, Load);
  and and_16 (and_16_out, Load, data_in[7]);
  and and_17 (and_17_out, register_value[8], not_25_out);
  not not_25 (not_25_out, Load);
  and and_18 (and_18_out, Load, data_in[8]);
  and and_19 (and_19_out, register_value[9], not_26_out);
  not not_26 (not_26_out, Load);
  and and_20 (and_20_out, Load, data_in[9]);
  and and_21 (and_21_out, register_value[10], not_27_out);
  not not_27 (not_27_out, Load);
  and and_22 (and_22_out, Load, data_in[10]);
  and and_23 (and_23_out, register_value[11], not_28_out);
  not not_28 (not_28_out, Load);
  and and_24 (and_24_out, Load, data_in[11]);
  and and_25 (and_25_out, register_value[12], not_29_out);
  not not_29 (not_29_out, Load);
  and and_26 (and_26_out, Load, data_in[12]);
  and and_27 (and_27_out, register_value[13], not_30_out);
  not not_30 (not_30_out, Load);
  and and_28 (and_28_out, Load, data_in[13]);
  and and_29 (and_29_out, register_value[14], not_31_out);
  not not_31 (not_31_out, Load);
  and and_30 (and_30_out, Load, data_in[14]);
  and and_31 (and_31_out, register_value[15], not_32_out);
  not not_32 (not_32_out, Load);
  and and_32 (and_32_out, Load, data_in[15]);
  and and_33 (and_33_out, register_value[16], not_1_out);
  and and_34 (and_34_out, Load, data_in[16]);
  and and_35 (and_35_out, register_value[17], not_2_out);
  and and_36 (and_36_out, Load, data_in[17]);
  and and_37 (and_37_out, register_value[18], not_3_out);
  and and_38 (and_38_out, Load, data_in[18]);
  and and_39 (and_39_out, register_value[19], not_4_out);
  and and_40 (and_40_out, Load, data_in[19]);
  and and_41 (and_41_out, register_value[20], not_5_out);
  and and_42 (and_42_out, Load, data_in[20]);
  and and_43 (and_43_out, register_value[21], not_6_out);
  and and_44 (and_44_out, Load, data_in[21]);
  and and_45 (and_45_out, register_value[22], not_7_out);
  and and_46 (and_46_out, Load, data_in[22]);
  and and_47 (and_47_out, register_value[23], not_8_out);
  and and_48 (and_48_out, Load, data_in[23]);
  and and_49 (and_49_out, register_value[24], not_9_out);
  and and_50 (and_50_out, Load, data_in[24]);
  and and_51 (and_51_out, register_value[25], not_10_out);
  and and_52 (and_52_out, Load, data_in[25]);
  and and_53 (and_53_out, register_value[26], not_11_out);
  and and_54 (and_54_out, Load, data_in[26]);
  and and_55 (and_55_out, register_value[27], not_12_out);
  and and_56 (and_56_out, Load, data_in[27]);
  and and_57 (and_57_out, register_value[28], not_13_out);
  and and_58 (and_58_out, Load, data_in[28]);
  and and_59 (and_59_out, register_value[29], not_14_out);
  and and_60 (and_60_out, Load, data_in[29]);
  and and_61 (and_61_out, register_value[30], not_15_out);
  and and_62 (and_62_out, Load, data_in[30]);
  and and_63 (and_63_out, register_value[31], not_16_out);
  and and_64 (and_64_out, Load, data_in[31]);
  or or_1 (or_1_out, and_1_out, and_2_out);
  or or_2 (or_2_out, and_3_out, and_4_out);
  or or_3 (or_3_out, and_5_out, and_6_out);
  or or_4 (or_4_out, and_7_out, and_8_out);
  or or_5 (or_5_out, and_9_out, and_10_out);
  or or_6 (or_6_out, and_11_out, and_12_out);
  or or_7 (or_7_out, and_13_out, and_14_out);
  or or_8 (or_8_out, and_15_out, and_16_out);
  or or_9 (or_9_out, and_17_out, and_18_out);
  or or_10 (or_10_out, and_19_out, and_20_out);
  or or_11 (or_11_out, and_21_out, and_22_out);
  or or_12 (or_12_out, and_23_out, and_24_out);
  or or_13 (or_13_out, and_25_out, and_26_out);
  or or_14 (or_14_out, and_27_out, and_28_out);
  or or_15 (or_15_out, and_29_out, and_30_out);
  or or_16 (or_16_out, and_31_out, and_32_out);
  or or_17 (or_17_out, and_33_out, and_34_out);
  or or_18 (or_18_out, and_35_out, and_36_out);
  or or_19 (or_19_out, and_37_out, and_38_out);
  or or_20 (or_20_out, and_39_out, and_40_out);
  or or_21 (or_21_out, and_41_out, and_42_out);
  or or_22 (or_22_out, and_43_out, and_44_out);
  or or_23 (or_23_out, and_45_out, and_46_out);
  or or_24 (or_24_out, and_47_out, and_48_out);
  or or_25 (or_25_out, and_49_out, and_50_out);
  or or_26 (or_26_out, and_51_out, and_52_out);
  or or_27 (or_27_out, and_53_out, and_54_out);
  or or_28 (or_28_out, and_55_out, and_56_out);
  or or_29 (or_29_out, and_57_out, and_58_out);
  or or_30 (or_30_out, and_59_out, and_60_out);
  or or_31 (or_31_out, and_61_out, and_62_out);
  or or_32 (or_32_out, and_63_out, and_64_out);
  D_Flip_Flop d_ff_1 (.clk(clk), .D(or_1_out), .Q(register_value[0]));  // open: Qn, preset, en, reset
  D_Flip_Flop d_ff_2 (.clk(clk), .D(or_2_out), .Q(register_value[1]));  // open: Qn, preset, en, reset
  D_Flip_Flop d_ff_3 (.clk(clk), .D(or_3_out), .Q(register_value[2]));  // open: Qn, preset, en, reset
  D_Flip_Flop d_ff_4 (.clk(clk), .D(or_4_out), .Q(register_value[3]));  // open: Qn, preset, en, reset
  D_Flip_Flop d_ff_5 (.clk(clk), .D(or_5_out), .Q(register_value[4]));  // open: Qn, preset, en, reset
  D_Flip_Flop d_ff_6 (.clk(clk), .D(or_6_out), .Q(register_value[5]));  // open: Qn, preset, en, reset
  D_Flip_Flop d_ff_7 (.clk(clk), .D(or_7_out), .Q(register_value[6]));  // open: Qn, preset, en, reset
  D_Flip_Flop d_ff_8 (.clk(clk), .D(or_8_out), .Q(register_value[7]));  // open: Qn, preset, en, reset
  D_Flip_Flop d_ff_9 (.clk(clk), .D(or_9_out), .Q(register_value[8]));  // open: Qn, preset, en, reset
  D_Flip_Flop d_ff_10 (.clk(clk), .D(or_10_out), .Q(register_value[9]));  // open: Qn, preset, en, reset
  D_Flip_Flop d_ff_11 (.clk(clk), .D(or_11_out), .Q(register_value[10]));  // open: Qn, preset, en, reset
  D_Flip_Flop d_ff_12 (.clk(clk), .D(or_12_out), .Q(register_value[11]));  // open: Qn, preset, en, reset
  D_Flip_Flop d_ff_13 (.clk(clk), .D(or_13_out), .Q(register_value[12]));  // open: Qn, preset, en, reset
  D_Flip_Flop d_ff_14 (.clk(clk), .D(or_14_out), .Q(register_value[13]));  // open: Qn, preset, en, reset
  D_Flip_Flop d_ff_15 (.clk(clk), .D(or_15_out), .Q(register_value[14]));  // open: Qn, preset, en, reset
  D_Flip_Flop d_ff_16 (.clk(clk), .D(or_16_out), .Q(register_value[15]));  // open: Qn, preset, en, reset
  D_Flip_Flop d_ff_17 (.clk(clk), .D(or_17_out), .Q(register_value[16]));  // open: Qn, preset, en, reset
  D_Flip_Flop d_ff_18 (.clk(clk), .D(or_18_out), .Q(register_value[17]));  // open: Qn, preset, en, reset
  D_Flip_Flop d_ff_19 (.clk(clk), .D(or_19_out), .Q(register_value[18]));  // open: Qn, preset, en, reset
  D_Flip_Flop d_ff_20 (.clk(clk), .D(or_20_out), .Q(register_value[19]));  // open: Qn, preset, en, reset
  D_Flip_Flop d_ff_21 (.clk(clk), .D(or_21_out), .Q(register_value[20]));  // open: Qn, preset, en, reset
  D_Flip_Flop d_ff_22 (.clk(clk), .D(or_22_out), .Q(register_value[21]));  // open: Qn, preset, en, reset
  D_Flip_Flop d_ff_23 (.clk(clk), .D(or_23_out), .Q(register_value[22]));  // open: Qn, preset, en, reset
  D_Flip_Flop d_ff_24 (.clk(clk), .D(or_24_out), .Q(register_value[23]));  // open: Qn, preset, en, reset
  D_Flip_Flop d_ff_25 (.clk(clk), .D(or_25_out), .Q(register_value[24]));  // open: Qn, preset, en, reset
  D_Flip_Flop d_ff_26 (.clk(clk), .D(or_26_out), .Q(register_value[25]));  // open: Qn, preset, en, reset
  D_Flip_Flop d_ff_27 (.clk(clk), .D(or_27_out), .Q(register_value[26]));  // open: Qn, preset, en, reset
  D_Flip_Flop d_ff_28 (.clk(clk), .D(or_28_out), .Q(register_value[27]));  // open: Qn, preset, en, reset
  D_Flip_Flop d_ff_29 (.clk(clk), .D(or_29_out), .Q(register_value[28]));  // open: Qn, preset, en, reset
  D_Flip_Flop d_ff_30 (.clk(clk), .D(or_30_out), .Q(register_value[29]));  // open: Qn, preset, en, reset
  D_Flip_Flop d_ff_31 (.clk(clk), .D(or_31_out), .Q(register_value[30]));  // open: Qn, preset, en, reset
  D_Flip_Flop d_ff_32 (.clk(clk), .D(or_32_out), .Q(register_value[31]));  // open: Qn, preset, en, reset

  // Notes on the sheet:
  //   Load
  //   Data_in
  //   Load
  //   Data_in
  //   Load
  //   Data_in
  //   Load
  //   Data_in
  //   Load
  //   Data_in
  //   Load
  //   Data_in
  //   Load
  //   Data_in
  //   Load
  //   Data_in
  //   Load
  //   Data_in
  //   Load
  //   Data_in
  //   Load
  //   Data_in
  //   Load
  //   Data_in
  //   Load
  //   Data_in
  //   Load
  //   Data_in
  //   Load
  //   Data_in
  //   Load
  //   Data_in
  //   Load
  //   Data_in
  //   Load
  //   Data_in
  //   Load
  //   Data_in
  //   Load
  //   Data_in
  //   Load
  //   Data_in
  //   Load
  //   Data_in
  //   Load
  //   Data_in
  //   Load
  //   Data_in
  //   Load
  //   Data_in
  //   Load
  //   Data_in
  //   Load
  //   Data_in
  //   Load
  //   Data_in
  //   Load
  //   Data_in
  //   Load
  //   Data_in
  //   Load
  //   Data_in
  //   Load
  //   Data_in
endmodule

module register_file (
  input  [2:0] rs_or_rt_3bit_read,
  input  [2:0] rs_or_rt_3bit_read_2,
  input  [31:0] data_in,
  input  RegWrite,
  input  [2:0] rd_or_rt_3bit_write,
  input  clk,
  output [31:0] clk_2,
  output [31:0] clk_3
);

  wire and_1_out, and_2_out, and_3_out, and_4_out, and_5_out, and_6_out, and_7_out, and_8_out,
       decoder_1_out0, decoder_1_out1, decoder_1_out2, decoder_1_out3, decoder_1_out4, decoder_1_out5,
       decoder_1_out6, decoder_1_out7;
  wire [31:0] Register__0_register_value, Register__1_register_value, Register__2_register_value,
       Register__3_register_value, Register__4_register_value, Register__5_register_value,
       Register__6_register_value, Register__7_register_value;

  Decoder #(.select(3), .enable("false")) decoder_1 (
    .out0(decoder_1_out0), .out1(decoder_1_out1), .out2(decoder_1_out2), .out3(decoder_1_out3),
    .out4(decoder_1_out4), .out5(decoder_1_out5), .out6(decoder_1_out6), .out7(decoder_1_out7),
    .sel(rd_or_rt_3bit_write));
  single_32bit_register Register__0 (
    .data_in(data_in), .Load(and_1_out), .register_value(Register__0_register_value), .clk(clk));
  and and_1 (and_1_out, decoder_1_out0, RegWrite);
  single_32bit_register Register__1 (
    .data_in(data_in), .Load(and_2_out), .register_value(Register__1_register_value), .clk(clk));
  and and_2 (and_2_out, decoder_1_out1, RegWrite);
  single_32bit_register Register__2 (
    .data_in(data_in), .Load(and_3_out), .register_value(Register__2_register_value), .clk(clk));
  and and_3 (and_3_out, decoder_1_out2, RegWrite);
  single_32bit_register Register__3 (
    .data_in(data_in), .Load(and_4_out), .register_value(Register__3_register_value), .clk(clk));
  and and_4 (and_4_out, decoder_1_out3, RegWrite);
  single_32bit_register Register__4 (
    .data_in(data_in), .Load(and_5_out), .register_value(Register__4_register_value), .clk(clk));
  and and_5 (and_5_out, decoder_1_out4, RegWrite);
  single_32bit_register Register__5 (
    .data_in(data_in), .Load(and_6_out), .register_value(Register__5_register_value), .clk(clk));
  and and_6 (and_6_out, decoder_1_out5, RegWrite);
  single_32bit_register Register__6 (
    .data_in(data_in), .Load(and_7_out), .register_value(Register__6_register_value), .clk(clk));
  and and_7 (and_7_out, decoder_1_out6, RegWrite);
  single_32bit_register Register__7 (
    .data_in(data_in), .Load(and_8_out), .register_value(Register__7_register_value), .clk(clk));
  and and_8 (and_8_out, decoder_1_out7, RegWrite);
  Multiplexer #(.select(3), .width(32), .enable("false")) multiplexer_1 (
    .in0(Register__0_register_value), .in1(Register__1_register_value), .in2(Register__2_register_value),
    .in3(Register__3_register_value), .in4(Register__4_register_value), .in5(Register__5_register_value),
    .in6(Register__6_register_value), .in7(Register__7_register_value), .out(clk_3), .sel(rs_or_rt_3bit_read));
  Multiplexer #(.select(3), .width(32), .enable("false")) multiplexer_2 (
    .in0(Register__0_register_value), .in1(Register__1_register_value), .in2(Register__2_register_value),
    .in3(Register__3_register_value), .in4(Register__4_register_value), .in5(Register__5_register_value),
    .in6(Register__6_register_value), .in7(Register__7_register_value), .out(clk_2),
    .sel(rs_or_rt_3bit_read_2));
endmodule

module _1_bit_Logic_unit (
  input  [1:0] LOGICAL_OP,
  input  _1st_operand,
  input  _2nd_operand,
  output logical_unit_output
);

  wire and_1_out, not_1_out, or_1_out, xor_1_out, xor_2_out;

  xor xor_1 (xor_1_out, _1st_operand, _2nd_operand);
  and and_1 (and_1_out, _1st_operand, _2nd_operand);
  or or_1 (or_1_out, _1st_operand, _2nd_operand);
  xor xor_2 (xor_2_out, _1st_operand, _2nd_operand);
  not not_1 (not_1_out, xor_1_out);
  Multiplexer #(.select(2), .enable("false")) multiplexer_1 (
    .in0(and_1_out), .in1(or_1_out), .in2(xor_2_out), .in3(not_1_out), .out(logical_unit_output),
    .sel(LOGICAL_OP));
endmodule

module _1_bit_Arithmetic_unit (
  input  c_in,
  input  _1st_operand,
  input  _2nd_operand,
  input  ARITHMETIC_OP,
  output sum,
  output c_out
);

  wire xor_1_out;

  xor xor_1 (xor_1_out, _2nd_operand, ARITHMETIC_OP);
  Adder #(.width(1)) adder_1 (.a(_1st_operand), .b(xor_1_out), .out(sum), .cin(c_in), .cout(c_out));
endmodule

module _1_bit_ALU (
  input  _2nd_operand,
  input  _1st_operand,
  input  ARITHMETIC_OP,
  input  [1:0] LOGICAL_OP,
  input  c_in,
  output arth_output,
  output carry,
  output logic_output
);

  _1_bit_Arithmetic_unit u_1_bit_arithmetic_unit_1 (
    ._1st_operand(_1st_operand), ._2nd_operand(_2nd_operand), .ARITHMETIC_OP(ARITHMETIC_OP),
    .sum(arth_output), .c_out(carry), .c_in(c_in));
  _1_bit_Logic_unit u_1_bit_logic_unit_1 (
    .logical_unit_output(logic_output), ._1st_operand(_1st_operand), ._2nd_operand(_2nd_operand),
    .LOGICAL_OP(LOGICAL_OP));
endmodule

module _32_bit_ALU_Unit (
  input  [7:0] ALU_CONTROL,
  input  [31:0] A,
  input  [31:0] B,
  output [31:0] ALU_output,
  output Overflow_flag,
  output sign_flag,
  output Zero_flag
);

  wire multiplexer_1_out, n1_bit_alu_1_carry, n1_bit_alu_2_carry, n1_bit_alu_3_carry, n1_bit_alu_4_carry,
       n1_bit_alu_5_carry, n1_bit_alu_6_carry, n1_bit_alu_7_carry, n1_bit_alu_8_carry, n1_bit_alu_9_carry,
       n1_bit_alu_10_carry, n1_bit_alu_11_carry, n1_bit_alu_12_carry, n1_bit_alu_13_carry,
       n1_bit_alu_14_carry, n1_bit_alu_15_carry, n1_bit_alu_16_carry, n1_bit_alu_17_carry,
       n1_bit_alu_18_carry, n1_bit_alu_19_carry, n1_bit_alu_20_carry, n1_bit_alu_21_carry,
       n1_bit_alu_22_carry, n1_bit_alu_23_carry, n1_bit_alu_24_carry, n1_bit_alu_25_carry,
       n1_bit_alu_26_carry, n1_bit_alu_27_carry, n1_bit_alu_28_carry, n1_bit_alu_29_carry,
       n1_bit_alu_30_carry, n1_bit_alu_31_carry, n1_bit_alu_32_carry, or_1_out;
  wire [30:0] n1_bit_alu_1_arth_output;
  wire [31:0] bit_extender_1_out, n1_bit_alu_1_logic_output, shift_unit_1_shifter_output;

  Shift_unit shift_unit_1 (
    .A(A), .shift_amount_imm_5(B[4:0]), .shifter_output(shift_unit_1_shifter_output),
    .SHIFT_TYPE(ALU_CONTROL[7:6]));
  _1_bit_ALU u_1_bit_alu_1 (
    .arth_output(n1_bit_alu_1_arth_output[0]), .carry(n1_bit_alu_1_carry),
    .logic_output(n1_bit_alu_1_logic_output[0]), ._2nd_operand(B[0]), ._1st_operand(A[0]),
    .ARITHMETIC_OP(ALU_CONTROL[3]), .LOGICAL_OP(ALU_CONTROL[5:4]), .c_in(ALU_CONTROL[3]));
  _1_bit_ALU u_1_bit_alu_2 (
    .arth_output(n1_bit_alu_1_arth_output[1]), .carry(n1_bit_alu_2_carry),
    .logic_output(n1_bit_alu_1_logic_output[1]), ._2nd_operand(B[1]), ._1st_operand(A[1]),
    .ARITHMETIC_OP(ALU_CONTROL[3]), .LOGICAL_OP(ALU_CONTROL[5:4]), .c_in(n1_bit_alu_1_carry));
  _1_bit_ALU u_1_bit_alu_3 (
    .arth_output(n1_bit_alu_1_arth_output[2]), .carry(n1_bit_alu_3_carry),
    .logic_output(n1_bit_alu_1_logic_output[2]), ._2nd_operand(B[2]), ._1st_operand(A[2]),
    .ARITHMETIC_OP(ALU_CONTROL[3]), .LOGICAL_OP(ALU_CONTROL[5:4]), .c_in(n1_bit_alu_2_carry));
  _1_bit_ALU u_1_bit_alu_4 (
    .arth_output(n1_bit_alu_1_arth_output[3]), .carry(n1_bit_alu_4_carry),
    .logic_output(n1_bit_alu_1_logic_output[3]), ._2nd_operand(B[3]), ._1st_operand(A[3]),
    .ARITHMETIC_OP(ALU_CONTROL[3]), .LOGICAL_OP(ALU_CONTROL[5:4]), .c_in(n1_bit_alu_3_carry));
  _1_bit_ALU u_1_bit_alu_5 (
    .arth_output(n1_bit_alu_1_arth_output[4]), .carry(n1_bit_alu_5_carry),
    .logic_output(n1_bit_alu_1_logic_output[4]), ._2nd_operand(B[4]), ._1st_operand(A[4]),
    .ARITHMETIC_OP(ALU_CONTROL[3]), .LOGICAL_OP(ALU_CONTROL[5:4]), .c_in(n1_bit_alu_4_carry));
  _1_bit_ALU u_1_bit_alu_6 (
    .arth_output(n1_bit_alu_1_arth_output[5]), .carry(n1_bit_alu_6_carry),
    .logic_output(n1_bit_alu_1_logic_output[5]), ._2nd_operand(B[5]), ._1st_operand(A[5]),
    .ARITHMETIC_OP(ALU_CONTROL[3]), .LOGICAL_OP(ALU_CONTROL[5:4]), .c_in(n1_bit_alu_5_carry));
  _1_bit_ALU u_1_bit_alu_7 (
    .arth_output(n1_bit_alu_1_arth_output[6]), .carry(n1_bit_alu_7_carry),
    .logic_output(n1_bit_alu_1_logic_output[6]), ._2nd_operand(B[6]), ._1st_operand(A[6]),
    .ARITHMETIC_OP(ALU_CONTROL[3]), .LOGICAL_OP(ALU_CONTROL[5:4]), .c_in(n1_bit_alu_6_carry));
  _1_bit_ALU u_1_bit_alu_8 (
    .arth_output(n1_bit_alu_1_arth_output[7]), .carry(n1_bit_alu_8_carry),
    .logic_output(n1_bit_alu_1_logic_output[7]), ._2nd_operand(B[7]), ._1st_operand(A[7]),
    .ARITHMETIC_OP(ALU_CONTROL[3]), .LOGICAL_OP(ALU_CONTROL[5:4]), .c_in(n1_bit_alu_7_carry));
  _1_bit_ALU u_1_bit_alu_9 (
    .arth_output(n1_bit_alu_1_arth_output[8]), .carry(n1_bit_alu_9_carry),
    .logic_output(n1_bit_alu_1_logic_output[8]), ._2nd_operand(B[8]), ._1st_operand(A[8]),
    .ARITHMETIC_OP(ALU_CONTROL[3]), .LOGICAL_OP(ALU_CONTROL[5:4]), .c_in(n1_bit_alu_8_carry));
  _1_bit_ALU u_1_bit_alu_10 (
    .arth_output(n1_bit_alu_1_arth_output[9]), .carry(n1_bit_alu_10_carry),
    .logic_output(n1_bit_alu_1_logic_output[9]), ._2nd_operand(B[9]), ._1st_operand(A[9]),
    .ARITHMETIC_OP(ALU_CONTROL[3]), .LOGICAL_OP(ALU_CONTROL[5:4]), .c_in(n1_bit_alu_9_carry));
  _1_bit_ALU u_1_bit_alu_11 (
    .arth_output(n1_bit_alu_1_arth_output[10]), .carry(n1_bit_alu_11_carry),
    .logic_output(n1_bit_alu_1_logic_output[10]), ._2nd_operand(B[10]), ._1st_operand(A[10]),
    .ARITHMETIC_OP(ALU_CONTROL[3]), .LOGICAL_OP(ALU_CONTROL[5:4]), .c_in(n1_bit_alu_10_carry));
  _1_bit_ALU u_1_bit_alu_12 (
    .arth_output(n1_bit_alu_1_arth_output[11]), .carry(n1_bit_alu_12_carry),
    .logic_output(n1_bit_alu_1_logic_output[11]), ._2nd_operand(B[11]), ._1st_operand(A[11]),
    .ARITHMETIC_OP(ALU_CONTROL[3]), .LOGICAL_OP(ALU_CONTROL[5:4]), .c_in(n1_bit_alu_11_carry));
  _1_bit_ALU u_1_bit_alu_13 (
    .arth_output(n1_bit_alu_1_arth_output[12]), .carry(n1_bit_alu_13_carry),
    .logic_output(n1_bit_alu_1_logic_output[12]), ._2nd_operand(B[12]), ._1st_operand(A[12]),
    .ARITHMETIC_OP(ALU_CONTROL[3]), .LOGICAL_OP(ALU_CONTROL[5:4]), .c_in(n1_bit_alu_12_carry));
  _1_bit_ALU u_1_bit_alu_14 (
    .arth_output(n1_bit_alu_1_arth_output[13]), .carry(n1_bit_alu_14_carry),
    .logic_output(n1_bit_alu_1_logic_output[13]), ._2nd_operand(B[13]), ._1st_operand(A[13]),
    .ARITHMETIC_OP(ALU_CONTROL[3]), .LOGICAL_OP(ALU_CONTROL[5:4]), .c_in(n1_bit_alu_13_carry));
  _1_bit_ALU u_1_bit_alu_15 (
    .arth_output(n1_bit_alu_1_arth_output[14]), .carry(n1_bit_alu_15_carry),
    .logic_output(n1_bit_alu_1_logic_output[14]), ._2nd_operand(B[14]), ._1st_operand(A[14]),
    .ARITHMETIC_OP(ALU_CONTROL[3]), .LOGICAL_OP(ALU_CONTROL[5:4]), .c_in(n1_bit_alu_14_carry));
  _1_bit_ALU u_1_bit_alu_16 (
    .arth_output(n1_bit_alu_1_arth_output[15]), .carry(n1_bit_alu_16_carry),
    .logic_output(n1_bit_alu_1_logic_output[15]), ._2nd_operand(B[15]), ._1st_operand(A[15]),
    .ARITHMETIC_OP(ALU_CONTROL[3]), .LOGICAL_OP(ALU_CONTROL[5:4]), .c_in(n1_bit_alu_15_carry));
  _1_bit_ALU u_1_bit_alu_17 (
    .arth_output(n1_bit_alu_1_arth_output[16]), .carry(n1_bit_alu_17_carry),
    .logic_output(n1_bit_alu_1_logic_output[16]), ._2nd_operand(B[16]), ._1st_operand(A[16]),
    .ARITHMETIC_OP(ALU_CONTROL[3]), .LOGICAL_OP(ALU_CONTROL[5:4]), .c_in(n1_bit_alu_16_carry));
  _1_bit_ALU u_1_bit_alu_18 (
    .arth_output(n1_bit_alu_1_arth_output[17]), .carry(n1_bit_alu_18_carry),
    .logic_output(n1_bit_alu_1_logic_output[17]), ._2nd_operand(B[17]), ._1st_operand(A[17]),
    .ARITHMETIC_OP(ALU_CONTROL[3]), .LOGICAL_OP(ALU_CONTROL[5:4]), .c_in(n1_bit_alu_17_carry));
  _1_bit_ALU u_1_bit_alu_19 (
    .arth_output(n1_bit_alu_1_arth_output[18]), .carry(n1_bit_alu_19_carry),
    .logic_output(n1_bit_alu_1_logic_output[18]), ._2nd_operand(B[18]), ._1st_operand(A[18]),
    .ARITHMETIC_OP(ALU_CONTROL[3]), .LOGICAL_OP(ALU_CONTROL[5:4]), .c_in(n1_bit_alu_18_carry));
  _1_bit_ALU u_1_bit_alu_20 (
    .arth_output(n1_bit_alu_1_arth_output[19]), .carry(n1_bit_alu_20_carry),
    .logic_output(n1_bit_alu_1_logic_output[19]), ._2nd_operand(B[19]), ._1st_operand(A[19]),
    .ARITHMETIC_OP(ALU_CONTROL[3]), .LOGICAL_OP(ALU_CONTROL[5:4]), .c_in(n1_bit_alu_19_carry));
  _1_bit_ALU u_1_bit_alu_21 (
    .arth_output(n1_bit_alu_1_arth_output[20]), .carry(n1_bit_alu_21_carry),
    .logic_output(n1_bit_alu_1_logic_output[20]), ._2nd_operand(B[20]), ._1st_operand(A[20]),
    .ARITHMETIC_OP(ALU_CONTROL[3]), .LOGICAL_OP(ALU_CONTROL[5:4]), .c_in(n1_bit_alu_20_carry));
  _1_bit_ALU u_1_bit_alu_22 (
    .arth_output(n1_bit_alu_1_arth_output[21]), .carry(n1_bit_alu_22_carry),
    .logic_output(n1_bit_alu_1_logic_output[21]), ._2nd_operand(B[21]), ._1st_operand(A[21]),
    .ARITHMETIC_OP(ALU_CONTROL[3]), .LOGICAL_OP(ALU_CONTROL[5:4]), .c_in(n1_bit_alu_21_carry));
  _1_bit_ALU u_1_bit_alu_23 (
    .arth_output(n1_bit_alu_1_arth_output[22]), .carry(n1_bit_alu_23_carry),
    .logic_output(n1_bit_alu_1_logic_output[22]), ._2nd_operand(B[22]), ._1st_operand(A[22]),
    .ARITHMETIC_OP(ALU_CONTROL[3]), .LOGICAL_OP(ALU_CONTROL[5:4]), .c_in(n1_bit_alu_22_carry));
  _1_bit_ALU u_1_bit_alu_24 (
    .arth_output(n1_bit_alu_1_arth_output[23]), .carry(n1_bit_alu_24_carry),
    .logic_output(n1_bit_alu_1_logic_output[23]), ._2nd_operand(B[23]), ._1st_operand(A[23]),
    .ARITHMETIC_OP(ALU_CONTROL[3]), .LOGICAL_OP(ALU_CONTROL[5:4]), .c_in(n1_bit_alu_23_carry));
  _1_bit_ALU u_1_bit_alu_25 (
    .arth_output(n1_bit_alu_1_arth_output[24]), .carry(n1_bit_alu_25_carry),
    .logic_output(n1_bit_alu_1_logic_output[24]), ._2nd_operand(B[24]), ._1st_operand(A[24]),
    .ARITHMETIC_OP(ALU_CONTROL[3]), .LOGICAL_OP(ALU_CONTROL[5:4]), .c_in(n1_bit_alu_24_carry));
  _1_bit_ALU u_1_bit_alu_26 (
    .arth_output(n1_bit_alu_1_arth_output[25]), .carry(n1_bit_alu_26_carry),
    .logic_output(n1_bit_alu_1_logic_output[25]), ._2nd_operand(B[25]), ._1st_operand(A[25]),
    .ARITHMETIC_OP(ALU_CONTROL[3]), .LOGICAL_OP(ALU_CONTROL[5:4]), .c_in(n1_bit_alu_25_carry));
  _1_bit_ALU u_1_bit_alu_27 (
    .arth_output(n1_bit_alu_1_arth_output[26]), .carry(n1_bit_alu_27_carry),
    .logic_output(n1_bit_alu_1_logic_output[26]), ._2nd_operand(B[26]), ._1st_operand(A[26]),
    .ARITHMETIC_OP(ALU_CONTROL[3]), .LOGICAL_OP(ALU_CONTROL[5:4]), .c_in(n1_bit_alu_26_carry));
  _1_bit_ALU u_1_bit_alu_28 (
    .arth_output(n1_bit_alu_1_arth_output[27]), .carry(n1_bit_alu_28_carry),
    .logic_output(n1_bit_alu_1_logic_output[27]), ._2nd_operand(B[27]), ._1st_operand(A[27]),
    .ARITHMETIC_OP(ALU_CONTROL[3]), .LOGICAL_OP(ALU_CONTROL[5:4]), .c_in(n1_bit_alu_27_carry));
  _1_bit_ALU u_1_bit_alu_29 (
    .arth_output(n1_bit_alu_1_arth_output[28]), .carry(n1_bit_alu_29_carry),
    .logic_output(n1_bit_alu_1_logic_output[28]), ._2nd_operand(B[28]), ._1st_operand(A[28]),
    .ARITHMETIC_OP(ALU_CONTROL[3]), .LOGICAL_OP(ALU_CONTROL[5:4]), .c_in(n1_bit_alu_28_carry));
  _1_bit_ALU u_1_bit_alu_30 (
    .arth_output(n1_bit_alu_1_arth_output[29]), .carry(n1_bit_alu_30_carry),
    .logic_output(n1_bit_alu_1_logic_output[29]), ._2nd_operand(B[29]), ._1st_operand(A[29]),
    .ARITHMETIC_OP(ALU_CONTROL[3]), .LOGICAL_OP(ALU_CONTROL[5:4]), .c_in(n1_bit_alu_29_carry));
  _1_bit_ALU u_1_bit_alu_31 (
    .arth_output(n1_bit_alu_1_arth_output[30]), .carry(n1_bit_alu_31_carry),
    .logic_output(n1_bit_alu_1_logic_output[30]), ._2nd_operand(B[30]), ._1st_operand(A[30]),
    .ARITHMETIC_OP(ALU_CONTROL[3]), .LOGICAL_OP(ALU_CONTROL[5:4]), .c_in(n1_bit_alu_30_carry));
  _1_bit_ALU u_1_bit_alu_32 (
    .arth_output(sign_flag), .carry(n1_bit_alu_32_carry), .logic_output(n1_bit_alu_1_logic_output[31]),
    ._2nd_operand(B[31]), ._1st_operand(A[31]), .ARITHMETIC_OP(ALU_CONTROL[3]),
    .LOGICAL_OP(ALU_CONTROL[5:4]), .c_in(n1_bit_alu_31_carry));
  xor xor_1 (Overflow_flag, n1_bit_alu_32_carry, n1_bit_alu_31_carry);
  or or_1 (or_1_out, n1_bit_alu_1_arth_output[0], n1_bit_alu_1_arth_output[1], n1_bit_alu_1_arth_output[2], n1_bit_alu_1_arth_output[3], n1_bit_alu_1_arth_output[4], n1_bit_alu_1_arth_output[5], n1_bit_alu_1_arth_output[6], n1_bit_alu_1_arth_output[7], n1_bit_alu_1_arth_output[8], n1_bit_alu_1_arth_output[9], n1_bit_alu_1_arth_output[10], n1_bit_alu_1_arth_output[11], n1_bit_alu_1_arth_output[12], n1_bit_alu_1_arth_output[13], n1_bit_alu_1_arth_output[14], n1_bit_alu_1_arth_output[15], n1_bit_alu_1_arth_output[16], n1_bit_alu_1_arth_output[17], n1_bit_alu_1_arth_output[18], n1_bit_alu_1_arth_output[19], n1_bit_alu_1_arth_output[20], n1_bit_alu_1_arth_output[21], n1_bit_alu_1_arth_output[22], n1_bit_alu_1_arth_output[23], n1_bit_alu_1_arth_output[24], n1_bit_alu_1_arth_output[25], n1_bit_alu_1_arth_output[26], n1_bit_alu_1_arth_output[27], n1_bit_alu_1_arth_output[28], n1_bit_alu_1_arth_output[29], n1_bit_alu_1_arth_output[30], sign_flag);
  not not_1 (Zero_flag, or_1_out);
  assign bit_extender_1_out = {{31{1'b0}}, multiplexer_1_out};  // Bit_Extender bit_extender_1
  Multiplexer #(.enable("false")) multiplexer_1 (
    .in0(sign_flag), .in1(Zero_flag), .out(multiplexer_1_out), .sel(ALU_CONTROL[0]));
  Multiplexer #(.select(2), .width(32), .enable("false")) multiplexer_2 (
    .in0(shift_unit_1_shifter_output), .in1(bit_extender_1_out), .in2({sign_flag, n1_bit_alu_1_arth_output}),
    .in3(n1_bit_alu_1_logic_output), .out(ALU_output), .sel(ALU_CONTROL[2:1]));
endmodule

module Data_memory (
  input  [31:0] data_in,
  input  [31:0] Address_in,
  input  MEM_WRITE,
  input  MEM_READ,
  input  clk,
  output [31:0] data_out
);

  RAM #(.addrWidth(20), .dataWidth(32), .bus("separate")) ram_1 (
    .addr(Address_in[19:0]), .din(data_in), .data(data_out), .str(MEM_WRITE), .clk(clk), .ld(MEM_READ));  // open: sel, clr
endmodule

module Main_Control (
  input  [1:0] function_2bit,
  input  [4:0] Op_code_5bit,
  output REG_READ_RA,
  output REG_READ_RB,
  output LINK_REG,
  output REG_WRITE,
  output EXT_OP,
  output EXT_TYPE,
  output [1:0] ALU_SRC,
  output [7:0] ALU_CONTROL,
  output MEM_READ,
  output MEM_WRITE,
  output SET_TYPE,
  output [1:0] REG_SRC,
  output [2:0] BRANCH_TYPE,
  output BRANCH_IMM_TYPE,
  output J,
  output [1:0] PC_SRC,
  output BRANCH_JUMP
);

  wire Add, ADDI, AND, ANDI, BEQ, BEQZ, BGEZ, BGTZ, BLEZ, BLTZ, BNE, BNEZ, decoder_1_out0, decoder_1_out1,
       decoder_1_out2, decoder_1_out3, decoder_2_out0, decoder_2_out1, decoder_2_out2, decoder_2_out3,
       decoder_3_out0, decoder_3_out1, EQV, EQVI, J_t, JAL, JALR, JR, OR, ORI, SEQ, SEQI, SET, SLL, SLt,
       SLTI, Sub, XOR, XORI;

  and and_1 (OR, decoder_1_out1, decoder_3_out0);
  and and_2 (AND, decoder_1_out0, decoder_3_out0);
  and and_3 (EQV, decoder_1_out3, decoder_3_out0);
  and and_4 (XOR, decoder_1_out2, decoder_3_out0);
  Decoder #(.select(2)) decoder_1 (
    .out0(decoder_1_out0), .out1(decoder_1_out1), .out2(decoder_1_out2), .out3(decoder_1_out3),
    .sel(function_2bit), .en(1'b1));
  and and_5 (Add, decoder_2_out0, decoder_3_out1);
  and and_6 (Sub, decoder_2_out1, decoder_3_out1);
  and and_7 (SEQ, decoder_2_out3, decoder_3_out1);
  and and_8 (SLt, decoder_2_out2, decoder_3_out1);
  Decoder #(.select(2)) decoder_2 (
    .out0(decoder_2_out0), .out1(decoder_2_out1), .out2(decoder_2_out2), .out3(decoder_2_out3),
    .sel(function_2bit), .en(1'b1));
  or or_1 (ALU_CONTROL[1], AND, OR, XOR, EQV, SLt, SEQ, ANDI, ORI, XORI, EQVI, SLTI, SEQI);
  or or_2 (ALU_CONTROL[5], XOR, EQV, XORI, EQVI);
  or or_3 (ALU_CONTROL[0], SEQ, SEQI);
  or or_4 (ALU_CONTROL[2], AND, OR, XOR, EQV, Add, Sub, ANDI, ORI, XORI, EQVI, ADDI, MEM_READ, MEM_WRITE, JR, JALR);
  Decoder #(.select(5), .enable("false")) decoder_3 (
    .out0(decoder_3_out0), .out1(decoder_3_out1), .out4(ANDI), .out5(ORI), .out6(XORI), .out7(EQVI),
    .out8(ADDI), .out9(SLTI), .out10(SEQI), .out11(SLL), .out12(ALU_CONTROL[6]), .out13(ALU_CONTROL[7]),
    .out14(BEQ), .out15(BNE), .out16(MEM_READ), .out17(MEM_WRITE), .out20(BEQZ), .out21(BNEZ), .out22(BLTZ),
    .out23(BGEZ), .out24(BGTZ), .out25(BLEZ), .out26(JR), .out27(JALR), .out28(SET), .out29(SET_TYPE),
    .out30(J_t), .out31(JAL), .sel(Op_code_5bit));  // open: out2, out3, out18, out19
  or or_5 (ALU_CONTROL[3], Sub, SLt, SEQ, SLTI, SEQI, BEQ, BNE, BEQZ, BNEZ, BLTZ, BGEZ, BGTZ, BLEZ);
  or or_6 (REG_READ_RB, BEQ, BNE, MEM_WRITE);
  or or_7 (ALU_SRC[0], ANDI, ORI, XORI, EQVI, ADDI, SLTI, SEQI, SLL, ALU_CONTROL[6], ALU_CONTROL[7], MEM_READ, MEM_WRITE, BEQZ, BNEZ, BLTZ, BGEZ, BGTZ, BLEZ, JR, JALR);
  or or_8 (EXT_OP, ADDI, SLTI, SEQI, MEM_READ, MEM_WRITE, JR, JALR, SET);
  nor nor_1 (REG_WRITE, BEQ, BNE, MEM_WRITE, BEQZ, BNEZ, BLTZ, BGEZ, BGTZ, BLEZ, JR, J_t);
  or or_9 (ALU_CONTROL[4], SLTI, SEQI, BEQZ, BNEZ, BLTZ, BGEZ, BGTZ, BLEZ);
  or or_10 (BRANCH_TYPE[0], BNE, BNEZ, BGEZ, BLEZ);
  or or_11 (REG_READ_RA, BEQZ, BNEZ, BLTZ, BGEZ, BGTZ, BLEZ, JR, JALR, SET_TYPE);
  or or_12 (ALU_SRC[1], BEQZ, BNEZ, BLTZ, BGEZ, BGTZ, BLEZ, SET_TYPE);
  or or_13 (BRANCH_TYPE[1], BEQZ, BNEZ, BGTZ, BLEZ);
  or or_14 (BRANCH_TYPE[2], BLTZ, BGEZ, BGTZ, BLEZ);
  or or_15 (BRANCH_IMM_TYPE, BEQZ, BNEZ, BLTZ, BGEZ, BGTZ, BLEZ);
  or or_16 (PC_SRC[0], BEQ, BNE, BEQZ, BNEZ, BLTZ, BGEZ, BGTZ, BLEZ, J_t, JAL);
  or or_17 (BRANCH_JUMP, BEQ, BNE, BEQZ, BNEZ, BLTZ, BGEZ, BGTZ, BLEZ, JR, JALR, J_t, JAL);
  or or_18 (REG_SRC[1], MEM_READ, JAL);
  or or_19 (LINK_REG, JALR, JAL);
  or or_20 (EXT_TYPE, JR, JALR, SET, SET_TYPE);
  or or_21 (PC_SRC[1], JR, JALR);
  or or_22 (J, JR, JALR, J_t, JAL);
  or or_23 (REG_SRC[0], SET, SET_TYPE, JAL);

  // Other names for the same wires on the sheet: SRL = ALU_CONTROL[6]; ROR = ALU_CONTROL[7]; LW = MEM_READ;
  //   SSET = SET_TYPE; SW = MEM_WRITE
endmodule

module Next_PC_Unit (
  input  [19:0] pc_1,
  input  [7:0] branch_imm_8,
  input  J,
  input  branch_output,
  input  BRANCH_IMM_TYPE,
  input  [10:0] jump_imm_11,
  output [19:0] next_pc
);

  wire [19:0] adder_1_out, adder_2_out, bit_extender_1_out, bit_extender_2_out, bit_extender_3_out,
       multiplexer_1_out, multiplexer_2_out;

  assign bit_extender_1_out = {{15{branch_imm_8[4]}}, branch_imm_8[4:0]};  // Bit_Extender bit_extender_1
  assign bit_extender_2_out = {{12{branch_imm_8[7]}}, branch_imm_8};  // Bit_Extender bit_extender_2
  assign bit_extender_3_out = {{9{jump_imm_11[10]}}, jump_imm_11};  // Bit_Extender bit_extender_3
  Multiplexer #(.width(20), .enable("false")) multiplexer_1 (
    .in0(bit_extender_1_out), .in1(bit_extender_2_out), .out(multiplexer_1_out), .sel(BRANCH_IMM_TYPE));
  Adder #(.width(20)) adder_1 (.a(pc_1), .b(multiplexer_1_out), .out(adder_1_out), .cin(1'b0));  // open: cout
  Multiplexer #(.width(20), .enable("false")) multiplexer_2 (
    .in0(pc_1), .in1(adder_1_out), .out(multiplexer_2_out), .sel(branch_output));
  Adder #(.width(20)) adder_2 (.a(pc_1), .b(bit_extender_3_out), .out(adder_2_out), .cin(1'b0));  // open: cout
  Multiplexer #(.width(20), .enable("false")) multiplexer_3 (
    .in0(multiplexer_2_out), .in1(adder_2_out), .out(next_pc), .sel(J));
endmodule

module Extend_Unit (
  input  EXT_OP,
  input  [7:0] imm_in,
  input  EXT_TYPE,
  output [31:0] Extended_output
);

  wire and_1_out, and_2_out;
  wire [31:0] bit_extender_1_out, bit_extender_2_out;

  and and_1 (and_1_out, imm_in[4], EXT_OP);
  assign bit_extender_1_out = {{27{and_1_out}}, imm_in[4:0]};  // Bit_Extender bit_extender_1
  and and_2 (and_2_out, imm_in[7], EXT_OP);
  assign bit_extender_2_out = {{24{and_2_out}}, imm_in};  // Bit_Extender bit_extender_2
  Multiplexer #(.width(32), .enable("false")) multiplexer_1 (
    .in0(bit_extender_1_out), .in1(bit_extender_2_out), .out(Extended_output), .sel(EXT_TYPE));

  // Notes on the sheet:
  //   imm(5)_sign_bit
  //   imm(8)_sign_bit
endmodule

module Set_unit (
  input  [31:0] Extended_imm8,
  input  SET_TYPE,
  input  [31:0] Alu_shifted_output,
  output [31:0] Set_output
);

  wire [31:0] multiplexer_1_out;

  Multiplexer #(.width(32), .enable("false")) multiplexer_1 (
    .in0({32{1'b0}}), .in1(Alu_shifted_output), .out(multiplexer_1_out), .sel(SET_TYPE));
  Adder #(.width(32)) adder_1 (.a(Extended_imm8), .b(multiplexer_1_out), .out(Set_output), .cin(1'b0));  // open: cout
endmodule

module Shift_unit (
  input  [31:0] A,
  input  [4:0] shift_amount_imm_5,
  input  [1:0] SHIFT_TYPE,
  output [31:0] shifter_output
);

  wire [31:0] shifter_1_out, shifter_2_out, shifter_3_out;

  Shifter #(.width(32)) shifter_1 (.in(A), .\dist (shift_amount_imm_5), .out(shifter_1_out));
  Shifter #(.width(32), .shift("lr")) shifter_2 (.in(A), .\dist (shift_amount_imm_5), .out(shifter_2_out));
  Shifter #(.width(32), .shift("rr")) shifter_3 (.in(A), .\dist (shift_amount_imm_5), .out(shifter_3_out));
  Multiplexer #(.select(2), .width(32), .enable("false")) multiplexer_1 (
    .in0(shifter_1_out), .in1(shifter_2_out), .in2(shifter_3_out), .in3({32{1'b0}}), .out(shifter_output),
    .sel(SHIFT_TYPE));
endmodule

module Branch_Unit (
  input  zero_flag,
  input  sign_flag,
  input  [2:0] BRANCH_TYPE,
  output branch_output
);

  wire and_1_out, and_2_out, not_1_out, not_2_out, not_3_out, not_4_out, or_1_out, or_2_out;

  not not_1 (not_1_out, zero_flag);
  not not_2 (not_2_out, sign_flag);
  not not_3 (not_3_out, zero_flag);
  and and_1 (and_1_out, not_1_out, sign_flag);
  and and_2 (and_2_out, not_2_out, not_1_out);
  not not_4 (not_4_out, zero_flag);
  or or_1 (or_1_out, and_1_out, zero_flag);
  or or_2 (or_2_out, and_2_out, zero_flag);
  Multiplexer #(.select(3), .enable("false")) multiplexer_1 (
    .in0(zero_flag), .in1(not_4_out), .in2(zero_flag), .in3(not_3_out), .in4(and_1_out), .in5(or_2_out),
    .in6(and_2_out), .in7(or_1_out), .out(branch_output), .sel(BRANCH_TYPE));

  // Notes on the sheet:
  //   BEQ
  //   BNE
  //   BEQZ
  //   BNEZ
  //   BLTZ
  //   BLEZ
  //   BGTZ
  //   BGEZ
endmodule

module IF_ID (
  input  [19:0] pc_1,
  input  Clear,
  input  [15:0] instruction,
  input  clk,
  output [19:0] pc_1_2,
  output [10:0] imm_11,
  output [7:0] imm_5_8,
  output [1:0] fn,
  output [2:0] Rt,
  output [2:0] Rs,
  output [2:0] Rd,
  output [4:0] OP_code
);

  Register #(.width(20)) register_1 (.D(pc_1), .Q(pc_1_2), .clk(clk), .clr(Clear));  // open: en
  Register #(.width(16)) register_2 (
    .D(instruction), .Q({OP_code, imm_11[10:8], imm_5_8[7:2], fn}), .clk(clk), .clr(Clear));  // open: en

  assign imm_5_8[1:0] = fn;
  assign imm_11[7:0] = {imm_5_8[7:2], fn};
  assign Rd = imm_11[10:8];
  assign Rs = imm_5_8[7:5];
  assign Rt = imm_5_8[4:2];
endmodule

module ID_EX (
  input  [19:0] pc_1,
  input  [10:0] imm11,
  input  [7:0] imm_5_8,
  input  [31:0] A,
  input  [31:0] B,
  input  [2:0] dest_reg,
  input  [2:0] BRANCH_TYPE,
  input  BRANCH_IMM_TYPE,
  input  J,
  input  [1:0] PC_SRC,
  input  REG_WRITE,
  input  EXT_OP,
  input  EXT_TYPE,
  input  [1:0] ALU_SRC,
  input  [7:0] ALU_CONTROL,
  input  MEM_READ,
  input  MEM_WRITE,
  input  SET_TYPE,
  input  [1:0] REG_SRC,
  input  [2:0] RA,
  input  [2:0] RB,
  input  clk,
  input  zeroing_control_singals,
  output [19:0] pc_1_2,
  output [10:0] imm11_2,
  output [7:0] imm_5_8_2,
  output [31:0] A_2,
  output [31:0] B_2,
  output [2:0] dest_reg_2,
  output [2:0] BRANCH_TYPE_2,
  output BRANCH_IMM_TYPE_2,
  output J_2,
  output [1:0] PC_SRC_2,
  output REG_WRITE_2,
  output EXT_OP_2,
  output EXT_TYPE_2,
  output [1:0] ALU_SRC_2,
  output [7:0] ALU_CONTROL_2,
  output MEM_READ_2,
  output MEM_WRITE_2,
  output SET_TYPE_2,
  output [1:0] REG_SRC_2,
  output [2:0] RA_2,
  output [2:0] RB_2
);

  Register #(.width(20)) register_1 (.D(pc_1), .Q(pc_1_2), .clk(clk));  // open: en, clr
  Register #(.width(11)) register_2 (.D(imm11), .Q(imm11_2), .clk(clk));  // open: en, clr
  Register register_3 (.D(imm_5_8), .Q(imm_5_8_2), .clk(clk));  // open: en, clr
  Register #(.width(32)) register_4 (.D(A), .Q(A_2), .clk(clk));  // open: en, clr
  Register #(.width(32)) register_5 (.D(B), .Q(B_2), .clk(clk));  // open: en, clr
  Register #(.width(3)) register_6 (.D(dest_reg), .Q(dest_reg_2), .clk(clk));  // open: en, clr
  Register #(.width(3)) register_7 (
    .D(BRANCH_TYPE), .Q(BRANCH_TYPE_2), .clk(clk), .clr(zeroing_control_singals));  // open: en
  Register #(.width(1)) register_8 (
    .D(BRANCH_IMM_TYPE), .Q(BRANCH_IMM_TYPE_2), .clk(clk), .clr(zeroing_control_singals));  // open: en
  Register #(.width(1)) register_9 (.D(J), .Q(J_2), .clk(clk), .clr(zeroing_control_singals));  // open: en
  Register #(.width(2)) register_10 (.D(PC_SRC), .Q(PC_SRC_2), .clk(clk), .clr(zeroing_control_singals));  // open: en
  Register #(.width(1)) register_11 (
    .D(REG_WRITE), .Q(REG_WRITE_2), .clk(clk), .clr(zeroing_control_singals));  // open: en
  Register #(.width(1)) register_12 (.D(EXT_OP), .Q(EXT_OP_2), .clk(clk), .clr(zeroing_control_singals));  // open: en
  Register #(.width(1)) register_13 (
    .D(EXT_TYPE), .Q(EXT_TYPE_2), .clk(clk), .clr(zeroing_control_singals));  // open: en
  Register #(.width(2)) register_14 (.D(ALU_SRC), .Q(ALU_SRC_2), .clk(clk), .clr(zeroing_control_singals));  // open: en
  Register register_15 (.D(ALU_CONTROL), .Q(ALU_CONTROL_2), .clk(clk), .clr(zeroing_control_singals));  // open: en
  Register #(.width(1)) register_16 (
    .D(MEM_READ), .Q(MEM_READ_2), .clk(clk), .clr(zeroing_control_singals));  // open: en
  Register #(.width(1)) register_17 (
    .D(MEM_WRITE), .Q(MEM_WRITE_2), .clk(clk), .clr(zeroing_control_singals));  // open: en
  Register #(.width(1)) register_18 (
    .D(SET_TYPE), .Q(SET_TYPE_2), .clk(clk), .clr(zeroing_control_singals));  // open: en
  Register #(.width(2)) register_19 (.D(REG_SRC), .Q(REG_SRC_2), .clk(clk), .clr(zeroing_control_singals));  // open: en
  Register #(.width(3)) register_20 (.D(RA), .Q(RA_2), .clk(clk), .clr(zeroing_control_singals));  // open: en
  Register #(.width(3)) register_21 (.D(RB), .Q(RB_2), .clk(clk), .clr(zeroing_control_singals));  // open: en
endmodule

module EX_MEM (
  input  [19:0] PC_2,
  input  [31:0] set_unit_output,
  input  [31:0] ALU_output,
  input  [31:0] sw_data,
  input  [2:0] dest_reg,
  input  REG_WRITE,
  input  MEM_READ,
  input  MEM_WRITE,
  input  [1:0] REG_SRC,
  input  clk,
  output [19:0] PC_2_2,
  output [31:0] set_unit_output_2,
  output [31:0] ALU_output_2,
  output [31:0] sw_data_2,
  output [2:0] dest_reg_2,
  output REG_WRITE_2,
  output MEM_READ_2,
  output MEM_WRITE_2,
  output [1:0] REG_SRC_2
);

  Register #(.width(20)) register_1 (.D(PC_2), .Q(PC_2_2), .clk(clk));  // open: en, clr
  Register #(.width(32)) register_2 (.D(set_unit_output), .Q(set_unit_output_2), .clk(clk));  // open: en, clr
  Register #(.width(32)) register_3 (.D(ALU_output), .Q(ALU_output_2), .clk(clk));  // open: en, clr
  Register #(.width(32)) register_4 (.D(sw_data), .Q(sw_data_2), .clk(clk));  // open: en, clr
  Register #(.width(3)) register_5 (.D(dest_reg), .Q(dest_reg_2), .clk(clk));  // open: en, clr
  Register #(.width(1)) register_6 (.D(REG_WRITE), .Q(REG_WRITE_2), .clk(clk));  // open: en, clr
  Register #(.width(1)) register_7 (.D(MEM_READ), .Q(MEM_READ_2), .clk(clk));  // open: en, clr
  Register #(.width(1)) register_8 (.D(MEM_WRITE), .Q(MEM_WRITE_2), .clk(clk));  // open: en, clr
  Register #(.width(2)) register_9 (.D(REG_SRC), .Q(REG_SRC_2), .clk(clk));  // open: en, clr
endmodule

module MEM_WB (
  input  [31:0] set_unit_output,
  input  [31:0] ALU_output,
  input  [31:0] extended_PC_2,
  input  [31:0] data_out,
  input  [2:0] dest_reg,
  input  REG_WRITE,
  input  [1:0] REG_SRC,
  input  clk,
  output [31:0] set_unit_output_2,
  output [31:0] ALU_output_2,
  output [31:0] extended_PC_2_2,
  output [31:0] data_out_2,
  output [2:0] dest_reg_2,
  output REG_WRITE_2,
  output [1:0] REG_SRC_2
);

  Register #(.width(32)) register_1 (.D(set_unit_output), .Q(set_unit_output_2), .clk(clk));  // open: en, clr
  Register #(.width(32)) register_2 (.D(ALU_output), .Q(ALU_output_2), .clk(clk));  // open: en, clr
  Register #(.width(32)) register_3 (.D(extended_PC_2), .Q(extended_PC_2_2), .clk(clk));  // open: en, clr
  Register #(.width(32)) register_4 (.D(data_out), .Q(data_out_2), .clk(clk));  // open: en, clr
  Register #(.width(3)) register_5 (.D(dest_reg), .Q(dest_reg_2), .clk(clk));  // open: en, clr
  Register #(.width(1)) register_6 (.D(REG_WRITE), .Q(REG_WRITE_2), .clk(clk));  // open: en, clr
  Register #(.width(2)) register_7 (.D(REG_SRC), .Q(REG_SRC_2), .clk(clk));  // open: en, clr
endmodule

module Forwarding_Unit (
  input  [2:0] EX_MEM_dest_reg,
  input  [2:0] ID_EX_RA,
  input  EX_MEM_REGWRITE,
  input  MEM_WB_REGWRITE,
  input  [2:0] MEM_WB_dest_reg,
  input  [2:0] ID_EX_RB,
  input  [1:0] ALU_SRC,
  input  EX_MEM_MEM_READ,
  output [2:0] ForwardA,
  output [2:0] ForwardB
);

  wire and_5_out, and_6_out, comparator_1_eq, comparator_2_eq, comparator_3_eq, comparator_4_eq,
       comparator_5_eq;
  wire [0:0] and_2_out, and_4_out;
  wire [1:0] or_1_out, or_2_out;
  wire [1:1] and_1_out, and_3_out;

  Comparator #(.width(3)) comparator_1 (.a(EX_MEM_dest_reg), .b(ID_EX_RA), .eq(comparator_1_eq));  // open: gt, lt
  Comparator #(.width(3)) comparator_2 (.a(ID_EX_RA), .b(MEM_WB_dest_reg), .eq(comparator_2_eq));  // open: gt, lt
  Comparator #(.width(3)) comparator_3 (.a(EX_MEM_dest_reg), .b(ID_EX_RB), .eq(comparator_3_eq));  // open: gt, lt
  Comparator #(.width(3)) comparator_4 (.a(ID_EX_RB), .b(MEM_WB_dest_reg), .eq(comparator_4_eq));  // open: gt, lt
  Comparator #(.width(2)) comparator_5 (.a(ALU_SRC), .b(2'b00), .eq(comparator_5_eq));  // open: gt, lt
  and and_1 (and_1_out[1], comparator_3_eq, comparator_5_eq, EX_MEM_REGWRITE);
  and and_2 (and_2_out[0], MEM_WB_REGWRITE, comparator_5_eq, comparator_4_eq);
  and and_3 (and_3_out[1], comparator_1_eq, EX_MEM_REGWRITE);
  and and_4 (and_4_out[0], MEM_WB_REGWRITE, comparator_2_eq);
  assign or_1_out = {and_3_out[1], 1'b0} | {1'b0, and_4_out[0]};  // OR_Gate or_1, 2 bits wide
  assign or_2_out = {and_1_out[1], 1'b0} | {1'b0, and_2_out[0]};  // OR_Gate or_2, 2 bits wide
  Multiplexer #(.width(3), .enable("false")) multiplexer_1 (
    .in0({1'b0, or_1_out}), .in1(3'b100), .out(ForwardA), .sel(and_5_out));
  and and_5 (and_5_out, comparator_1_eq, EX_MEM_MEM_READ);
  Multiplexer #(.width(3), .enable("false")) multiplexer_2 (
    .in0({1'b0, or_2_out}), .in1(3'b100), .out(ForwardB), .sel(and_6_out));
  and and_6 (and_6_out, comparator_3_eq, comparator_5_eq, EX_MEM_MEM_READ);
endmodule

module Hazard_detection_unit (
  input  ID_EX_MEM_READ,
  input  [2:0] IF_ID_RA,
  input  [2:0] ID_EX_dest_reg,
  input  [2:0] IF_ID_RB,
  input  [1:0] IF_ID_ALU_SRC,
  input  BRANCH_JUMP,
  input  clk,
  output Disable_IF_ID,
  output Disable_PC,
  output zeroing_control_signals
);

  wire and_1_out, and_2_out, comparator_1_eq, comparator_2_eq, comparator_3_eq, register_1_q, register_2_q,
       register_3_q;

  Comparator #(.width(3)) comparator_1 (.a(IF_ID_RA), .b(ID_EX_dest_reg), .eq(comparator_1_eq));  // open: gt, lt
  Comparator #(.width(3)) comparator_2 (.a(ID_EX_dest_reg), .b(IF_ID_RB), .eq(comparator_2_eq));  // open: gt, lt
  Comparator #(.width(2)) comparator_3 (.a(IF_ID_ALU_SRC), .b(2'b00), .eq(comparator_3_eq));  // open: gt, lt
  Register #(.width(1)) register_1 (.D(BRANCH_JUMP), .Q(register_1_q), .clk(clk));  // open: en, clr
  and and_1 (and_1_out, ID_EX_MEM_READ, comparator_1_eq);
  and and_2 (and_2_out, ID_EX_MEM_READ, comparator_3_eq, comparator_2_eq);
  Register #(.width(1)) register_2 (.D(register_1_q), .Q(register_2_q), .clk(clk));  // open: en, clr
  Register #(.width(1)) register_3 (.D(register_2_q), .Q(register_3_q), .clk(clk));  // open: en, clr
  or or_1 (Disable_IF_ID, and_1_out, and_2_out, register_2_q, register_3_q);

  assign Disable_PC = Disable_IF_ID;
  assign zeroing_control_signals = Disable_IF_ID;
endmodule

module Instruction_Memory (
  input  [19:0] next_pc,
  input  [1:0] PC_SRC,
  input  [19:0] ALU_output_20bitLSB,
  input  Enable,
  input  clk,
  output [19:0] PC_1,
  output [15:0] Instruction
);

  wire [19:0] multiplexer_1_out, register_1_q;

  Multiplexer #(.select(2), .width(20), .enable("false")) multiplexer_1 (
    .in0(PC_1), .in1(next_pc), .in2(ALU_output_20bitLSB), .out(multiplexer_1_out), .sel(PC_SRC));  // open: in3
  Register #(.width(20)) register_1 (.D(multiplexer_1_out), .en(Enable), .Q(register_1_q), .clk(clk));  // open: clr
  Adder #(.width(20)) adder_1 (.a(register_1_q), .b(20'h1), .out(PC_1), .cin(1'b0));  // open: cout
  RAM #(.addrWidth(20), .dataWidth(16)) ram_1 (
    .addr(register_1_q), .data(Instruction), .clk(clk), .ld(1'b1));  // open: sel, clr
endmodule

module test (
  input  clk,
  input  clk_2,
  input  clk_3,
  output clk_4
);

  Register #(.width(1)) register_1 (.D(clk), .Q(clk_4), .clk(clk_2), .clr(clk_3));  // open: en
endmodule
